# Fritzing sketch sketch (saved by Fritzing 0.9.3b)
breadboards: 1

parts:
  Part1 = Arduino Uno (Rev3)
  Part2 = InvenSense MPU6050
  LED1 = LED - 5mm [color="Red (633nm)" package="5 mm [THT]"]
  LED2 = LED - 5mm [color="Red (633nm)" package="5 mm [THT]"]
  R1 = Resistor [tolerance=±5% resistance=220 package=THT]
  R2 = Resistor [tolerance=±5% resistance=220 package=THT]
  J1 = Piezo Speaker
  R3 = Resistor [tolerance=±5% resistance=220 package=THT]

nets:
  N1: Part1.A4/SDA, Part2.SDA
  N2: Part1.A5/SCL, Part2.SCL
  N3: Part1.D9_PWM, J1.pin2
  N4: Part1.D2, Part2.INT
  N5: Part1.D4, LED1.anode
  N6: Part1.D7, LED2.anode
  5V: Part1.5V, Part2.VCC
  GND: Part1.GND, Part2.GND, Part2.AD0, R1.Pin_0, R2.Pin_0, R3.Pin_1
  N7: LED1.cathode, R1.Pin_1
  N8: LED2.cathode, R2.Pin_1
  N9: J1.pin1, R3.Pin_0
